# Fritzing sketch ServoArm Test (saved by Fritzing 0.9.3b)
breadboards: 1

parts:
  Part1 = Arduino Uno (Rev3)
  J1 = Basic Servo
  U1 = POT [package=pot_alpha_rv16af-20]

nets:
  N1: Part1.A0, U1.S
  N2: Part1.D9_PWM, J1.pulse
  5V: Part1.5V, J1.vcc, U1.A
  GND: Part1.GND, J1.gnd, U1.E
